# Fritzing sketch MK5 (saved by Fritzing 1.0.0rc)
breadboards: 1

parts:
  Part1 = RFID-RC522-v2
  Mod1 = Amica NodeMCU DEVKIT 1.0
  U1 = LCD-16X2 [package=lcd-16x2]
  LCM1602_IIC1 = LCM1602 IIC [part_number="LCM1602 IIC" chip_label="LCM1602 IIC" package="DIP (Dual Inline) [THT]"]
  Power_plug2 = Power plug
  L2 = Solenoid
  KY-1 = Keyes Relay [package=THT]

nets:
  N1: Part1.SDA, Mod1.pin_11
  N2: Part1.SCK, Mod1.pin8
  N3: Part1.MOSI, Mod1.pin6
  N4: Part1.MISO, Mod1.pin7
  GND: Part1.GND, Mod1.pin2, Mod1.pin_9, Mod1.pin_25, Mod1.pin_29, LCM1602_IIC1.GND, KY-1.ground
  N5: Part1.RST, Mod1.pin_12
  N6: Part1.3.3V, Mod1.pin1, Mod1.pin_10, Mod1.pin_26
  N7: Mod1.pin_13, LCM1602_IIC1.SDA
  N8: Mod1.pin_14, LCM1602_IIC1.SCL
  N9: Mod1.pin_15, KY-1.signal
  N10: Mod1.pin_30, LCM1602_IIC1.VCC, KY-1.power
  VSS: U1.VSS, LCM1602_IIC1.VSS
  VDD: U1.VDD, LCM1602_IIC1.VDD
  N11: U1.VO, LCM1602_IIC1.V0
  N12: U1.RS, LCM1602_IIC1.RS
  N13: U1.R_W, LCM1602_IIC1.RW
  N14: U1.E, LCM1602_IIC1.E
  N15: U1.DB0, LCM1602_IIC1.D0
  N16: U1.DB1, LCM1602_IIC1.D1
  N17: U1.DB2, LCM1602_IIC1.D2
  N18: U1.DB3, LCM1602_IIC1.D3
  N19: U1.DB4, LCM1602_IIC1.D4
  N20: U1.DB5, LCM1602_IIC1.D5
  N21: U1.DB6, LCM1602_IIC1.D6
  N22: U1.DB7, LCM1602_IIC1.D7
  N23: U1.A, LCM1602_IIC1.A
  N24: U1.K, LCM1602_IIC1.K
  N25: Power_plug2.GND, KY-1.C
  N26: Power_plug2.VCC, L2.pin1
  N27: L2.pin2, KY-1.NO

custom parts:
  RFID-RC522-v2: A simple China made RFID-RC522 Reader; do check the pin labels, as this is a MFRC522 based clone.
  LCM1602 IIC: I2C-Module to use a 1602 or 2004 LCD on with the wire.h libory Serial LCD Modul
  Keyes Relay: The Keyes 5V relay module is suitable for SCM development, home appliance control. It uses a 5V~12V TIL control signal which can control DC / AC signal.
